# Fritzing sketch Breadboard Arduino (saved by Fritzing 0.9.3b)
breadboards: 1

parts:
  S1 = Pushbutton [package="[THT]"]
  U1 = atmega328 [package=dip]
  R1 = Resistor [tolerance=±5% resistance=10k package="2010 [SMD]"]
  R2 = Resistor [tolerance=±5% resistance=1.2k package="2010 [SMD]"]
  LED_-_Flat_side_to_resistor = smd LED [color="Red (633nm)" package="1206 [SMD]"]
  XTAL1 = Crystal [frequency="16 Mhz" package=SMD]
  C4 = Ceramic Capacitor [capacitance="100 nF" package="0805 [SMD, multilayer]"]
  22pF = Ceramic Capacitor [capacitance=1µF package="100 mil [THT, multilayer]"]
  22pF_2 = Ceramic Capacitor [capacitance=1µF package="100 mil [THT, multilayer]"]

nets:
  N1: S1.Pin_1, S1.Pin_2, U1.RESET, R1.Pin_1, C4.1
  N2: S1.Pin_3, S1.Pin_4, U1.GND#21, R2.Pin_1
  N3: U1.GND#7, 22pF.1, 22pF_2.1
  N4: U1.XLAT1, XTAL1.pin_0, 22pF_2.0
  N5: U1.XLAT2, XTAL1.pin_1, 22pF.0
  N6: U1.D6_(PWM), LED_-_Flat_side_to_resistor.anode
  N7: U1.AVCC, R1.Pin_0
  N8: R2.Pin_0, LED_-_Flat_side_to_resistor.cathode

notes:
  DTR
  TXO
  RXI
